# Fritzing sketch hsl-busstop-sign (saved by Fritzing 0.9.3b)
breadboards: 1

parts:
  LCM1602_IIC2 = LCM1602 IIC [part_number="LCM1602 IIC" chip_label="LCM1602 IIC" package="DIP (Dual Inline) [THT]"]
  LCD1 = LCD screen
  R1 = Resistor [tolerance=±5% resistance=10k package="2512 [SMD]"]
  U1 = NodeMCU V1.0
  S1 = Pushbutton [package="[SMD]"]

nets:
  VSS: LCM1602_IIC2.VSS, LCD1.VSS
  VDD: LCM1602_IIC2.VDD, LCD1.VDD
  N1: LCM1602_IIC2.V0, LCD1.V0
  N2: LCM1602_IIC2.RS, LCD1.RS
  N3: LCM1602_IIC2.RW, LCD1.R/W
  N4: LCM1602_IIC2.E, LCD1.E
  N5: LCM1602_IIC2.D0, LCD1.DB0
  N6: LCM1602_IIC2.D1, LCD1.DB1
  N7: LCM1602_IIC2.D2, LCD1.DB2
  N8: LCM1602_IIC2.D3, LCD1.DB3
  N9: LCM1602_IIC2.D4, LCD1.DB4
  N10: LCM1602_IIC2.D5, LCD1.DB5
  N11: LCM1602_IIC2.D6, LCD1.DB6
  N12: LCM1602_IIC2.D7, LCD1.DB7
  N13: LCM1602_IIC2.A, LCD1.LED+
  N14: LCM1602_IIC2.K, LCD1.LED-
  GND: LCM1602_IIC2.GND, U1.GND
  N15: LCM1602_IIC2.VCC, R1.Pin_0
  N16: LCM1602_IIC2.SDA, U1.D4
  N17: LCM1602_IIC2.SCL, U1.D3
  N18: R1.Pin_1, U1.RST, S1.Pin_1, S1.Pin_2
  N19: S1.Pin_3, S1.Pin_4

custom parts:
  LCM1602 IIC: I2C-Module to use a 1602 or 2004 LCD on with the wire.h libory Serial LCD Modul
  NodeMCU V1.0: ESP8266 based NodeMCU
